# Fritzing sketch Lexin The Humanoid Robot (saved by Fritzing 0.9.9b)

parts:
  Mod1 = Raspberry Pi 4B
  VCC1 = Battery
  U1 = Voltage Regulator [package=to220-adj]
  TP1 = TP4056 [chip_label=TP4056 package="DIP (Dual Inline) [THT]"]
  U2 = NodeMCU V1.0
  USBTTL2 = USB TTL Serial Cable  # not connected
  S1 = H-Bridge with L298N
  M1 = gear-motor
  M2 = gear-motor

nets:
  N1: Mod1.5V, U1.OUT
  N2: Mod1.GND, VCC1.-, U1.IN, TP1.pin5
  N3: VCC1.+, U1.ADJ, TP1.pin4, S1.12V
  N4: U2.D5, S1.IN1
  N5: U2.D6, S1.IN2
  N6: U2.D7, S1.IN3
  N7: U2.D8, S1.IN4
  VIN: U2.Vin, S1.5V
  GND: U2.GND, S1.GND
  N8: S1.ENA, S1.ENA-5V
  N9: S1.ENB, S1.ENB-5V
  N10: S1.M1-01, M2.pin_2
  N11: S1.M1-02, M2.pin_1
  N12: S1.M2-01, M1.pin_2
  N13: S1.M2-02, M1.pin_1

notes:
  Charging Point
  Regular Microusb converter
  Connect speaker to 3.55MM audio jack
  L298N H Bridge Motor Driver
  5V Regulator
  Nodemcu Esp8266-12E
  TP4056 Charging Module
  Lithium Ion 3.7V Batteries x 2

custom parts:
  Battery: Your standard 2x 18650 battery pack (7,4 Volts)
  TP4056: A DIP stand-in part for whatever IC you want. With 6 pins on a 300mil dual inline package (DIP) footprint.
  NodeMCU V1.0: ESP8266 based NodeMCU
  H-Bridge with L298N: h-bridge
